# Fritzing sketch ADSWheather-NodeMCU (saved by Fritzing 0.9.3b)
breadboards: 1

parts:
  Componente1 = Adafruit ADS1115 16Bit I2C ADC [part_number="Adafruit #1085"]
  U1 = ESP8266 NodeMCU LoLin module
  J1 = RJ11 Jack [package=rj11-6]
  J2 = RJ11 Jack [package=rj11-6]
  J3 = RJ11 Jack [package=rj11-6]
  BATT1 = LiPoly Battery (1300mAh)
  R3 = Resistor [tolerance=±5% resistance=10 package="1206 [SMD]"]
  R4 = Resistor [tolerance=±5% resistance=10 package="1206 [SMD]"]
  R5 = Resistor [tolerance=±5% resistance=10 package="1206 [SMD]"]

nets:
  N1: Componente1.SDA, U1.D2
  N2: Componente1.SCL, U1.D1
  N3: U1.D3, J2.5, R4.Pin_0
  N4: U1.A0, J1.4, R3.Pin_0
  N5: J1.1, J2.2, J3.2, BATT1.negative
  N6: BATT1.positive, R3.Pin_1, R4.Pin_1, R5.Pin_1

notes:
  Veleta
  Anemómetro
  Pluviómetro
  El anemómetro se conecta mediante el RJ-11 a la veleta y de ahí al NodeMCU
  pin 2 - GND
  pin 3 - pin A2 (ADS1115)
  pin 4 - pin D4 (NodeMCU)
  pin 5 - Vdd

custom parts:
  Adafruit ADS1115 16Bit I2C ADC: For microcontrollers without an analog-to-digital converter or when you want a higher-precision ADC, the ADS1115 provides 16-bit precision at 860 samples/second over I2C. The chip can be configured as 4 single-ended input channels, or two differential channels. As a nice bonus, it even includes a programmable gain amplifier, up to x16, to help boost up smaller single/differential signals to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
  ESP8266 NodeMCU LoLin module: ESP8266 based NodeMCU
  LiPoly Battery (1300mAh): Lithium Ion Polymer Battery (1300mAh)
