# Fritzing sketch ADSWheather-NodeMCU_ESQUEMATICO (saved by Fritzing 0.9.3b)
breadboards: 1

parts:
  Componente1 = Adafruit ADS1115 16Bit I2C ADC [part_number="Adafruit #1085"]
  U1 = ESP8266 NodeMCU LoLin module
  J3 = RJ11 Jack [package=rj11-6]
  BATT1 = LiPoly Battery (1300mAh)
  R1 = Resistor [tolerance=±5% resistance=10k package="2512 [SMD]"]
  R2 = Resistor [tolerance=±5% resistance=10k package="2512 [SMD]"]
  J4 = RJ11 Jack [package=rj11-6]
  J5 = RJ11 Jack [package=rj11-6]
  R3 = Resistor [tolerance=±5% resistance=10k package="2512 [SMD]"]

nets:
  N1: Componente1.SDA, U1.D2
  N2: Componente1.SCL, U1.D1
  N3: Componente1.GND, BATT1.negative, J4.6
  N4: Componente1.VDD, BATT1.positive, R1.Pin_1
  N5: U1.D3, J5.3, R3.Pin_0
  N6: U1.D4, J3.3, R2.Pin_0
  N7: U1.A0, R1.Pin_0, J4.2

notes:
  Veleta
  Anemómetro
  Pluviómetro
  El anemómetro se conecta mediante el RJ-11 a la veleta y de ahí al NodeMCU
  pin 2 - GND
  pin 3 - pin A2 (ADS1115)
  pin 4 - pin D4 (NodeMCU)
  pin 5 - Vdd

custom parts:
  Adafruit ADS1115 16Bit I2C ADC: For microcontrollers without an analog-to-digital converter or when you want a higher-precision ADC, the ADS1115 provides 16-bit precision at 860 samples/second over I2C. The chip can be configured as 4 single-ended input channels, or two differential channels. As a nice bonus, it even includes a programmable gain amplifier, up to x16, to help boost up smaller single/differential signals to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
  ESP8266 NodeMCU LoLin module: ESP8266 based NodeMCU
  LiPoly Battery (1300mAh): Lithium Ion Polymer Battery (1300mAh)
