# Fritzing sketch Anemometro_NodeMCU (saved by Fritzing 0.9.3b)
breadboards: 1

parts:
  J1 = RJ11 Jack [package=rj11-6]
  U1 = ESP8266 NodeMCU LoLin module
  R1 = Resistor [tolerance=±5% resistance=10k package=THT]
  X1 = USB Connectors [package=usb-microb]  # not connected

nets:
  N1: J1.2, U1.D2, R1.Pin_1
  N2: J1.5, U1.GND
  N3: U1.3V3, R1.Pin_0

notes:
  Anemómetro

custom parts:
  ESP8266 NodeMCU LoLin module: ESP8266 based NodeMCU
