# Fritzing sketch BH1750-NodeMCU (saved by Fritzing 0.9.3b)
breadboards: 1

parts:
  Componente1 = BH1750
  U1 = ESP8266 NodeMCU LoLin module
  BATT1 = LiPoly Battery (1300mAh)
  X1 = USB Connectors [package=usb-microb]  # not connected

nets:
  N1: Componente1.VCC, BATT1.positive
  N2: Componente1.GND, BATT1.negative
  N3: Componente1.SCL, U1.D1
  N4: Componente1.SDA, U1.D2

notes:
  Si ADDR tiene un voltaje menor de 0,7V la dirección del sensor será 0x23. Si es mayor de 0,7V, será 0x5C
  3,3V
  5V

custom parts:
  BH1750: Light Sensor
  ESP8266 NodeMCU LoLin module: ESP8266 based NodeMCU
  LiPoly Battery (1300mAh): Lithium Ion Polymer Battery (1300mAh)
