# Fritzing sketch NodeMCU-Servidor (saved by Fritzing 0.9.3b)
breadboards: 1

parts:
  Componente1 = BME280 Breakout
  U1 = ESP8266 NodeMCU LoLin module
  U2 = LIPO-2000mAh [package=lipo-2000]
  X1 = USB Connectors [package=usb-minib]  # not connected
  YL-83_-_Detection_Board1 = YL-83 Rain Sensor - Detection Board
  YL-83_-_Control_Board1 = YL-83 Rain Sensor - Control Board
  R1 = Resistor [tolerance=±5% resistance=470 package="2512 [SMD]"]
  R2 = Resistor [tolerance=±5% resistance=470 package="2512 [SMD]"]
  PART1 = ML8511 UV Sensor Breakout [part_number=SEN-12705]  # not connected
  Componente2 = BH1750

nets:
  N1: Componente1.SDI/SDA, U1.D2
  N2: Componente1.SCK/SCL, U1.D1, Componente2.SCL
  N3: U1.D3, R2.Pin_0
  GND: U1.GND, U2.-, YL-83_-_Control_Board1.GND, R2.Pin_1, Componente2.GND
  VCC: U2.+, YL-83_-_Control_Board1.VCC, Componente2.VCC
  N4: YL-83_-_Detection_Board1.POS, YL-83_-_Control_Board1.POS
  N5: YL-83_-_Detection_Board1.NEG, YL-83_-_Control_Board1.NEG
  N6: YL-83_-_Control_Board1.AO, R1.Pin_0

notes:
  D1 - SCK - GPIO 4
  D2 SDI - GPIO 5
  5V

custom parts:
  ESP8266 NodeMCU LoLin module: ESP8266 based NodeMCU
  YL-83 Rain Sensor - Detection Board: The YL-83 is a rain sensor that has more resistance when dry and less resistance when wet. The module runs at 5V.
  YL-83 Rain Sensor - Control Board: The YL-83 is a rain sensor that has more resistance when dry and less resistance when wet. The module runs at 5V.
  ML8511 UV Sensor Breakout: Description: The ML8511 breakout is an easy to use ultraviolet light sensor. The MP8511 UV Sensor works by outputing an analog signal in relation to the amount of UV light it detects. This breakout can be very handy in creating devices that warn the user of sunburn or detect the UV index as it relates to weather conditions. This sensor breakout can detect 280-390nm light most effectively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
  BH1750: Light Sensor
