# Fritzing sketch BME280-NodeMCU (saved by Fritzing 0.9.3b)
breadboards: 1

parts:
  Componente1 = BME280 Breakout
  U1 = ESP8266 NodeMCU LoLin module
  BATT1 = LiPoly Battery (1300mAh)
  X1 = USB Connectors [package=usb-microb]  # not connected

nets:
  N1: Componente1.SDI/SDA, U1.D2
  N2: Componente1.SCK/SCL, U1.D1
  N3: U1.GND, BATT1.negative

notes:
  D1 - SCK - GPIO 4
  D2 SDI - GPIO 5
  5V

custom parts:
  ESP8266 NodeMCU LoLin module: ESP8266 based NodeMCU
  LiPoly Battery (1300mAh): Lithium Ion Polymer Battery (1300mAh)
