# Fritzing sketch ML8511_ADS1115ADC (saved by Fritzing 0.9.3b)
breadboards: 1

parts:
  U1 = ESP8266 NodeMCU LoLin module
  BATT1 = LiPoly Battery (1300mAh)  # not connected
  X1 = USB Connectors [package=usb-microb]  # not connected
  PART1 = ML8511 UV Sensor Breakout [part_number=SEN-12705]
  Componente1 = Adafruit ADS1115 16Bit I2C ADC [part_number="Adafruit #1085"]

nets:
  N1: U1.D1, Componente1.SCL
  N2: U1.D2, Componente1.SDA
  GND: U1.GND, PART1.GND, Componente1.ADDR, Componente1.GND
  N3: PART1.OUT, Componente1.AIN0
  N4: PART1.3.3V, Componente1.AIN1

notes:
  3,3V

custom parts:
  ESP8266 NodeMCU LoLin module: ESP8266 based NodeMCU
  LiPoly Battery (1300mAh): Lithium Ion Polymer Battery (1300mAh)
  ML8511 UV Sensor Breakout: Description: The ML8511 breakout is an easy to use ultraviolet light sensor. The MP8511 UV Sensor works by outputing an analog signal in relation to the amount of UV light it detects. This breakout can be very handy in creating devices that warn the user of sunburn or detect the UV index as it relates to weather conditions. This sensor breakout can detect 280-390nm light most effectively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
  Adafruit ADS1115 16Bit I2C ADC: For microcontrollers without an analog-to-digital converter or when you want a higher-precision ADC, the ADS1115 provides 16-bit precision at 860 samples/second over I2C. The chip can be configured as 4 single-ended input channels, or two differential channels. As a nice bonus, it even includes a programmable gain amplifier, up to x16, to help boost up smaller single/differential signals to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
